# Fritzing sketch Angle_and_Throw_Meter (saved by Fritzing 0.9.3b)
circuit board: 5.5cm x 3.3cm
breadboards: 1

parts:
  Arduino_Pro_Mini = Arduino Pro Mini v13
  R2 = Resistor [tolerance=±5% resistance=4.7k package=THT]
  Init = Pushbutton [package="[THT]"]
  Minus = Pushbutton [package="[THT]"]
  Plus = Pushbutton [package="[THT]"]
  Power = female pin header, 3 pins [form="♀ (female)"]
  Oled_164*32 = female pin header, 4 pins [form="♀ (female)"]
  R1 = Resistor [tolerance=±5% resistance=4.7k package=THT]
  R5 = Resistor [tolerance=±5% resistance=10k package=THT]
  R4 = Resistor [tolerance=±5% resistance=10k package=THT]
  R3 = Resistor [tolerance=±5% resistance=10k package=THT]
  ADXL345 = Triple Axis Accelerometer Breakout - ADXL345
  Programming = female pin header, 6 pins [form="♀ (female)"]

nets:
  N1: Arduino_Pro_Mini.DTR, Programming.pin1
  N2: Arduino_Pro_Mini.D0/TX, Programming.pin2
  N3: Arduino_Pro_Mini.D1/RX, Programming.pin3
  VCC: Arduino_Pro_Mini.VCC, R2.Pin_1, Oled_164*32.pin3, R1.Pin_1, R5.Pin_0, R4.Pin_0, R3.Pin_0, ADXL345.VCC, ADXL345.CS, Programming.pin4
  GND: Arduino_Pro_Mini.GND, Init.Pin_1, Init.Pin_2, Minus.Pin_1, Minus.Pin_2, Plus.Pin_1, Plus.Pin_2, Power.pin1, Power.pin3, Oled_164*32.pin4, ADXL345.GND, ADXL345.SDO, Programming.pin5, Programming.pin6
  N4: Arduino_Pro_Mini.A4, R2.Pin_0, Oled_164*32.pin1, ADXL345.SDA
  N5: Arduino_Pro_Mini.A5, Oled_164*32.pin2, R1.Pin_0, ADXL345.SCL
  N6: Arduino_Pro_Mini.RAW, Power.pin2
  N7: Arduino_Pro_Mini.D4, Init.Pin_3, Init.Pin_4, R3.Pin_1
  N8: Arduino_Pro_Mini.D3_PWM, Minus.Pin_3, Minus.Pin_4, R4.Pin_1
  N9: Arduino_Pro_Mini.D2, Plus.Pin_3, Plus.Pin_4, R5.Pin_1
